# Fritzing sketch ATtiny85 (saved by Fritzing 0.9.10b)
breadboards: 1

parts:
  U1 = ATTINY45 [package=dip]
  LED1 = smd LED [color="Red (633nm)" package="0805 [SMD]"]
  LED2 = smd LED [color="Red (633nm)" package="0805 [SMD]"]
  R1 = Resistor [tolerance=±5% resistance=220 package="0603 [SMD]"]
  R2 = Resistor [tolerance=±5% resistance=220 package="0603 [SMD]"]
  Part1 = Adafruit AVR 6-ISP Breakout [part_number="Adafruit #1465"]

nets:
  N1: U1.PB5(NRES), Part1.RST
  GND: U1.GND, LED1.cathode, LED2.cathode, Part1.GND
  N2: U1.PB0(MOSI), R2.Pin_0, Part1.MOSI
  N3: U1.PB1(MISO), R1.Pin_0, Part1.MISO
  N4: U1.PB2(SCK_ADC1), Part1.SCK
  VCC: U1.VCC, Part1.VCC
  N5: LED1.anode, R2.Pin_1
  N6: LED2.anode, R1.Pin_1

custom parts:
  Adafruit AVR 6-ISP Breakout: Programming AVR? Always Googling the pinout? Well, now no longer! It's rare to find a mini kit so elegant, it deserves its own Haiku. A simple breakout, 2x3 box header in the center, two 1x3's on the side. Plugs into any breadboard for neat wiring (in both nifty and clean senses of the word). Comes with a quality mini PCB, a 2x3 box header and a small stick of 0.1" header. Requires some light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
