# Fritzing sketch ArduinoUnoR3 (saved by Fritzing 0.9.10b)
breadboards: 1

parts:
  Part1 = Arduino Uno (Rev3) - ICSP
  LED1 = smd LED [color="Red (633nm)" package="0805 [SMD]"]
  LED2 = smd LED [color="Red (633nm)" package="0805 [SMD]"]
  R1 = Resistor [tolerance=±5% power=0.25 resistance=330 package=THT]
  R2 = Resistor [tolerance=±5% power=0.25 resistance=330 package=THT]

nets:
  N1: Part1.GND, LED1.cathode, LED2.cathode
  N2: Part1.D5_PWM, R1.Pin_0
  N3: Part1.D6_PWM, R2.Pin_0
  N4: LED1.anode, R2.Pin_1
  N5: LED2.anode, R1.Pin_1
